// Logisim project calc.circ as structural Verilog: 12 circuits, main circuit main
module main (
);

  wire DIV, MUL, n0, n1, n2, n3, n4, n5, n6, n7, n8, n9, num_to_bin_decoder_1_has_num_pressed,
       op_decoder_1_has_op_pressed, RESET, SUB, SUM, system_1_div_zero, system_1_is_negative_number;
  wire [2:0] op_decoder_1_op_code;
  wire [3:0] system_1_result_display_0, system_1_result_display_1;
  wire [7:0] num_to_bin_decoder_1_bin_num;

  Button button_1 (.out(n7));
  Button button_2 (.out(n4));
  Button button_3 (.out(n1));
  Button button_4 (.out(n8));
  Button button_5 (.out(n5));
  Button button_6 (.out(n2));
  Button button_7 (.out(n0));
  Button button_8 (.out(n9));
  Button button_9 (.out(n6));
  Button button_10 (.out(n3));
  NUM_TO_BIN_DECODER num_to_bin_decoder_1 (
    .N0(n0), .N1(n1), .N2(n2), .N3(n3), .N4(n4), .N5(n5), .N6(n6), .N7(n7), .N8(n8), .N9(n9),
    .BIN_NUM(num_to_bin_decoder_1_bin_num), .HAS_NUM_PRESSED(num_to_bin_decoder_1_has_num_pressed));
  OP_DECODER op_decoder_1 (
    .SUM(SUM), .SUB(SUB), .MUL(MUL), .DIV(DIV), .OP_CODE(op_decoder_1_op_code),
    .HAS_OP_PRESSED(op_decoder_1_has_op_pressed));
  Button button_11 (.out(SUM));
  Button button_12 (.out(SUB));
  Button button_13 (.out(MUL));
  Button button_14 (.out(DIV));
  Button button_15 (.out(RESET));
  SYSTEM system_1 (
    .RESET(RESET), .NUMBER(num_to_bin_decoder_1_bin_num),
    .HAS_NUM_PRESSED(num_to_bin_decoder_1_has_num_pressed), .OPERATION(op_decoder_1_op_code),
    .HAS_OP_PRESSED(op_decoder_1_has_op_pressed), .RESULT_DISPLAY_1(system_1_result_display_1),
    .RESULT_DISPLAY_0(system_1_result_display_0), .IS_NEGATIVE_NUMBER(system_1_is_negative_number),
    .DIV_ZERO(system_1_div_zero));
  _7_Segment_Display u_7_segment_display_1 (
    .g(system_1_div_zero), .f(system_1_div_zero), .a(system_1_div_zero), .b(1'b0), .e(system_1_div_zero),
    .d(system_1_div_zero), .c(1'b0), .dp(1'b0));
  _7_Segment_Display u_7_segment_display_2 (
    .g(system_1_is_negative_number), .f(1'b0), .a(1'b0), .b(1'b0), .e(1'b0), .d(1'b0), .c(1'b0), .dp(1'b0));
  Hex_Digit_Display hex_digit_display_1 (.value(system_1_result_display_1));  // open: dp
  Hex_Digit_Display hex_digit_display_2 (.value(system_1_result_display_0));  // open: dp

  // Notes on the sheet:
  //   7
  //   4
  //   1
  //   KEYBOARD
  //   8
  //   9
  //   5
  //   6
  //   2
  //   3
  //   0
  //   +
  //   -
  //   ×
  //   ÷
  //   C
  //   4 Basic Operations Calculator Between 2 Numbers
endmodule

module CONTROL (
  input  RESET,
  input  HAS_NUM_PRESSED,
  input  HAS_OP_PRESSED,
  input  EQUAL,
  input  CLK,
  output [1:0] FIRST_OR_SECOND
);

  wire combinational_1_d0, combinational_1_d1, combinational_1_d2;
  wire [2:0] sequential_1_q0;

  // Probe on sequential_1_q0
  COMBINATIONAL combinational_1 (
    .RESET(RESET), .HAS_NUM_PRESSED(HAS_NUM_PRESSED), .HAS_OP_PRESSED(HAS_OP_PRESSED), .EQUAL(EQUAL),
    .STATE(sequential_1_q0), .FIRST_OR_SECOND(FIRST_OR_SECOND), .D2(combinational_1_d2),
    .D1(combinational_1_d1), .D0(combinational_1_d0));  // open: CAN_CALCULATE
  SEQUENTIAL sequential_1 (
    .D2(combinational_1_d2), .D1(combinational_1_d1), .D0(combinational_1_d0), .CLK(CLK), .RST(RESET),
    .Q2(sequential_1_q0[2]), .Q1(sequential_1_q0[1]), .Q0(sequential_1_q0[0]));
endmodule

module NUM_TO_BIN_DECODER (
  input  N0,
  input  N1,
  input  N2,
  input  N3,
  input  N4,
  input  N5,
  input  N6,
  input  N7,
  input  N8,
  input  N9,
  output [7:0] BIN_NUM,
  output HAS_NUM_PRESSED
);

  or or_1 (BIN_NUM[0], N1, N3, N5, N7, N9);
  or or_2 (BIN_NUM[1], N2, N3, N6, N7);
  or or_3 (BIN_NUM[2], N4, N5, N6, N7);
  or or_4 (BIN_NUM[3], N8, N9);
  or or_5 (HAS_NUM_PRESSED, BIN_NUM[0], BIN_NUM[1], BIN_NUM[2], BIN_NUM[3], N0);

  assign BIN_NUM[7:4] = 4'b0000;
endmodule

module NUMBERS_MEMORY (
  input  [7:0] NUMBER,
  input  [1:0] FIRST_OR_SECOND,
  input  RESET_NUM_MEMORY,
  input  CLK,
  output [7:0] SAVED_NUM_1,
  output [7:0] SAVED_NUM_2
);

  wire and_1_out, and_2_out;

  and and_1 (and_1_out, FIRST_OR_SECOND[0], ~FIRST_OR_SECOND[1]);  // AND_Gate
  and and_2 (and_2_out, ~FIRST_OR_SECOND[0], FIRST_OR_SECOND[1]);  // AND_Gate
  Register register_1 (.D(NUMBER), .en(and_1_out), .clk(CLK), .Q(SAVED_NUM_1), .clr(RESET_NUM_MEMORY));
  Register register_2 (.D(NUMBER), .en(and_2_out), .clk(CLK), .Q(SAVED_NUM_2), .clr(RESET_NUM_MEMORY));
endmodule

module SYSTEM (
  input  RESET,
  input  [7:0] NUMBER,
  input  HAS_NUM_PRESSED,
  input  [2:0] OPERATION,
  input  HAS_OP_PRESSED,
  output [3:0] RESULT_DISPLAY_1,
  output [3:0] RESULT_DISPLAY_0,
  output IS_NEGATIVE_NUMBER,
  output DIV_ZERO
);

  wire clock_1_out, clock_2_out;
  wire [1:0] control_1_first_or_second;
  wire [2:0] register_1_q;

  Clock clock_1 (.out(clock_1_out));
  CONTROL control_1 (
    .RESET(RESET), .HAS_NUM_PRESSED(HAS_NUM_PRESSED), .HAS_OP_PRESSED(HAS_OP_PRESSED), .EQUAL(1'b0),
    .CLK(clock_1_out), .FIRST_OR_SECOND(control_1_first_or_second));
  Clock clock_2 (.out(clock_2_out));
  Register #(.width(3)) register_1 (
    .D(OPERATION), .en(HAS_OP_PRESSED), .clk(clock_2_out), .Q(register_1_q), .clr(RESET));
  DATAPATH datapath_1 (
    .OPERATION(register_1_q), .NUMBER(NUMBER), .FIRST_OR_SECOND(control_1_first_or_second),
    .RESET_NUM(RESET), .CLK(clock_1_out), .RESULT_DISPLAY_1(RESULT_DISPLAY_1),
    .RESULT_DISPLAY_0(RESULT_DISPLAY_0), .IS_NEGATIVE_NUMBER(IS_NEGATIVE_NUMBER), .DIV_ZERO(DIV_ZERO));
endmodule

module HAS_NUM_PRESSED (
  input  [4:0] HAS_NUM,
  output YES_OR_NO
);

  or or_1 (YES_OR_NO, HAS_NUM[0], HAS_NUM[1], HAS_NUM[2], HAS_NUM[3], HAS_NUM[4]);
endmodule

module OP_DECODER (
  input  SUM,
  input  SUB,
  input  MUL,
  input  DIV,
  output [2:0] OP_CODE,
  output HAS_OP_PRESSED
);

  wire and_1_out, and_2_out, and_3_out, and_4_out, not_1_out, not_2_out;

  not not_1 (not_1_out, SUB);
  not not_2 (not_2_out, DIV);
  or or_1 (HAS_OP_PRESSED, SUM, SUB, MUL, DIV);
  and and_1 (and_1_out, MUL, not_2_out);
  and and_2 (and_2_out, SUB, not_2_out);
  and and_3 (and_3_out, MUL, not_2_out);
  and and_4 (and_4_out, SUM, not_1_out, not_2_out);
  or or_2 (OP_CODE[1], and_1_out, and_2_out);
  or or_3 (OP_CODE[0], and_3_out, and_4_out);

  assign OP_CODE[2] = DIV;
endmodule

module MATH_OPS (
  input  [7:0] NUM_1,
  input  [7:0] NUM_2,
  input  [2:0] OPERATION,
  output [3:0] RESULT_DISPLAY_1,
  output [3:0] RESULT_DISPLAY_0,
  output HAS_NEGATIVE
);

  wire [6:0] subtractor_1_out;
  wire [7:0] adder_1_out, adder_2_out, divider_1_out, multiplexer_1_out, multiplexer_2_out, multiplier_1_out,
       not_1_out, SUBOP;

  Multiplexer #(.width(8)) multiplexer_1 (.in0({8{1'b0}}), .in1(NUM_2), .out(multiplexer_1_out), .sel(OPERATION[1]));
  Subtractor subtractor_1 (
    .a(NUM_1), .b(multiplexer_1_out), .out({HAS_NEGATIVE, subtractor_1_out}));  // open: bin, bout
  Adder adder_1 (.a(NUM_1), .b(NUM_2), .out(adder_1_out));  // open: cin, cout
  Multiplier multiplier_1 (.a(NUM_1), .b(NUM_2), .out(multiplier_1_out));  // open: cin, cout
  Divider divider_1 (.a(NUM_1), .b(NUM_2), .out(divider_1_out));  // open: upper, rem
  assign not_1_out = ~{HAS_NEGATIVE, subtractor_1_out};  // NOT_Gate not_1, 8 bits wide
  Adder adder_2 (.a(not_1_out), .b(8'h1), .out(adder_2_out));  // open: cin, cout
  Multiplexer #(.enable("true"), .select(3), .width(8)) multiplexer_2 (
    .in0(NUM_1), .in1(adder_1_out), .in2(SUBOP), .in3(multiplier_1_out), .in4(divider_1_out),
    .in5({8{1'b0}}), .in6({8{1'b0}}), .in7({8{1'b0}}), .out(multiplexer_2_out), .sel(OPERATION));  // open: en
  Multiplexer #(.enable("true"), .width(8)) multiplexer_3 (
    .in0({HAS_NEGATIVE, subtractor_1_out}), .in1(adder_2_out), .out(SUBOP), .sel(HAS_NEGATIVE));  // open: en
  // Binary_to_BCD_converter #(.binvalue(8)) binary_to_bcd_converter_1: pin names not known; wires that end beside it: multiplexer_2_out, RESULT_DISPLAY_1, RESULT_DISPLAY_0
  Hex_Digit_Display hex_digit_display_1 (.value(RESULT_DISPLAY_1));  // open: dp
  Hex_Digit_Display hex_digit_display_2 (.value(RESULT_DISPLAY_0));  // open: dp
endmodule

module ZERO_BY_ZERO_DIVISION (
  input  [7:0] NUM1,
  input  [7:0] NUM2,
  input  [2:0] DIV_OP,
  output IS_ZERO_BY_ZERO_DIV_ERR
);

  wire nor_1_out, nor_2_out;

  nor nor_1 (nor_1_out, NUM1[0], NUM1[1], NUM1[2], NUM1[3], NUM1[4], NUM1[5], NUM1[6], NUM1[7]);
  nor nor_2 (nor_2_out, NUM2[0], NUM2[1], NUM2[2], NUM2[3], NUM2[4], NUM2[5], NUM2[6], NUM2[7]);
  and and_1 (IS_ZERO_BY_ZERO_DIV_ERR, nor_1_out, nor_2_out, DIV_OP[2]);
endmodule

module SEQUENTIAL (
  input  D2,
  input  D1,
  input  D0,
  input  CLK,
  input  RST,
  output Q2,
  output Q1,
  output Q0
);

  D_Flip_Flop d_ff_1 (.D(D2), .clk(CLK), .Q(Q2), .reset(RST));  // open: Qn, preset
  D_Flip_Flop d_ff_2 (.D(D1), .clk(CLK), .Q(Q1), .reset(RST));  // open: Qn, preset
  D_Flip_Flop d_ff_3 (.D(D0), .clk(CLK), .Q(Q0), .reset(RST));  // open: Qn, preset
endmodule

module COMBINATIONAL (
  input  RESET,
  input  HAS_NUM_PRESSED,
  input  HAS_OP_PRESSED,
  input  EQUAL,
  input  [2:0] STATE,
  output [1:0] FIRST_OR_SECOND,
  output CAN_CALCULATE,
  output D2,
  output D1,
  output D0
);

  wire not_1_out, not_2_out, not_3_out, not_4_out, not_5_out, not_6_out, not_7_out, or_1_out, or_2_out,
       or_3_out, or_4_out, or_5_out, or_6_out, or_7_out, or_8_out, or_9_out, or_10_out, or_11_out, or_12_out,
       or_13_out, or_14_out, or_15_out, or_16_out, or_17_out, or_18_out, or_19_out, or_20_out, or_21_out,
       or_22_out, or_23_out, or_24_out;

  not not_1 (not_1_out, RESET);
  not not_2 (not_2_out, HAS_NUM_PRESSED);
  not not_3 (not_3_out, HAS_OP_PRESSED);
  not not_4 (not_4_out, EQUAL);
  not not_5 (not_5_out, STATE[2]);
  not not_6 (not_6_out, STATE[1]);
  not not_7 (not_7_out, STATE[0]);
  or or_1 (or_1_out, HAS_NUM_PRESSED, STATE[2]);
  or or_2 (or_2_out, not_2_out, not_5_out);
  or or_3 (or_3_out, not_3_out, not_4_out, not_7_out);
  or or_4 (or_4_out, HAS_NUM_PRESSED, not_7_out);
  or or_5 (or_5_out, HAS_NUM_PRESSED, not_4_out);
  or or_6 (or_6_out, HAS_NUM_PRESSED, not_3_out);
  or or_7 (or_7_out, HAS_NUM_PRESSED, STATE[1]);
  or or_8 (or_8_out, HAS_OP_PRESSED, EQUAL, STATE[0]);
  or or_9 (or_9_out, not_2_out, not_6_out);
  or or_10 (or_10_out, not_3_out, not_4_out, STATE[0]);
  or or_11 (or_11_out, HAS_NUM_PRESSED, EQUAL);
  or or_12 (or_12_out, not_6_out, STATE[0]);
  or or_13 (or_13_out, HAS_NUM_PRESSED, not_3_out);
  or or_14 (or_14_out, HAS_OP_PRESSED, EQUAL);
  or or_15 (or_15_out, HAS_NUM_PRESSED, not_3_out, STATE[2]);
  or or_16 (or_16_out, not_2_out, HAS_OP_PRESSED, STATE[2]);
  or or_17 (or_17_out, EQUAL, STATE[2]);
  or or_18 (or_18_out, EQUAL, STATE[2]);
  or or_19 (or_19_out, not_2_out, HAS_OP_PRESSED, STATE[2]);
  or or_20 (or_20_out, HAS_OP_PRESSED, STATE[1]);
  or or_21 (or_21_out, not_5_out, not_7_out);
  or or_22 (or_22_out, STATE[1], STATE[0]);
  or or_23 (or_23_out, HAS_NUM_PRESSED, STATE[0]);
  or or_24 (or_24_out, not_2_out, not_6_out);
  and and_1 (FIRST_OR_SECOND[1], or_1_out, STATE[1], or_2_out, or_3_out, not_1_out, or_4_out, or_5_out, or_6_out);
  and and_2 (FIRST_OR_SECOND[0], or_7_out, not_5_out, or_8_out, or_9_out, or_10_out, not_1_out, or_11_out, or_12_out, or_13_out);
  and and_3 (CAN_CALCULATE, or_14_out, STATE[1], not_7_out, or_15_out, or_16_out, or_17_out, not_1_out);
  and and_4 (D2, or_18_out, STATE[1], not_7_out, or_19_out, not_1_out);
  and and_5 (D1, or_20_out, or_21_out, or_22_out, not_1_out);
  and and_6 (D0, or_23_out, not_5_out, or_24_out, not_1_out);
endmodule

module DATAPATH (
  input  [2:0] OPERATION,
  input  [7:0] NUMBER,
  input  [1:0] FIRST_OR_SECOND,
  input  RESET_NUM,
  input  CLK,
  output [3:0] RESULT_DISPLAY_1,
  output [3:0] RESULT_DISPLAY_0,
  output IS_NEGATIVE_NUMBER,
  output DIV_ZERO
);

  wire [7:0] numbers_memory_1_saved_num_1, numbers_memory_1_saved_num_2;

  NUMBERS_MEMORY numbers_memory_1 (
    .NUMBER(NUMBER), .FIRST_OR_SECOND(FIRST_OR_SECOND), .RESET_NUM_MEMORY(RESET_NUM), .CLK(CLK),
    .SAVED_NUM_1(numbers_memory_1_saved_num_1), .SAVED_NUM_2(numbers_memory_1_saved_num_2));
  // Probe on numbers_memory_1_saved_num_1
  // Probe on numbers_memory_1_saved_num_2
  MATH_OPS math_ops_1 (
    .NUM_1(numbers_memory_1_saved_num_1), .NUM_2(numbers_memory_1_saved_num_2), .OPERATION(OPERATION),
    .RESULT_DISPLAY_1(RESULT_DISPLAY_1), .RESULT_DISPLAY_0(RESULT_DISPLAY_0),
    .HAS_NEGATIVE(IS_NEGATIVE_NUMBER));
  ZERO_BY_ZERO_DIVISION zero_by_zero_division_1 (
    .NUM1(numbers_memory_1_saved_num_1), .NUM2(numbers_memory_1_saved_num_2), .DIV_OP(OPERATION),
    .IS_ZERO_BY_ZERO_DIV_ERR(DIV_ZERO));
endmodule
